# Fritzing sketch robotichand (saved by Fritzing 0.9.3b)
breadboards: 1

parts:
  Part1 = Arduino Uno (Rev3)
  IC1 = Voltage Regulator [package=to-220-alt]
  J1 = Basic Servo
  J2 = Basic Servo
  J3 = Basic Servo
  J4 = Basic Servo
  R1 = Resistor [tolerance=±5% resistance=22k package=THT]
  R2 = Resistor [tolerance=±5% resistance=22k package=THT]
  R3 = Resistor [tolerance=±5% resistance=22k package=THT]
  R4 = Resistor [tolerance=±5% resistance=22k package=THT]
  R5 = Basic Flex Resistor
  R6 = Basic Flex Resistor
  R7 = Basic Flex Resistor
  R8 = Basic Flex Resistor
  BAT1 = LIPO-2000mAh [package=lipo-2000]

nets:
  N1: Part1.A0, R1.Pin_0, R8.Pin_2
  N2: Part1.A1, R2.Pin_0, R7.Pin_2
  N3: Part1.A2, R3.Pin_0, R6.Pin_2
  N4: Part1.A3, R4.Pin_0, R5.Pin_2
  N5: Part1.D9_PWM, J3.pulse
  N6: Part1.D10_PWM/SS, J4.pulse
  N7: Part1.GND, R1.Pin_1, R2.Pin_1, R3.Pin_1, R4.Pin_1
  N8: Part1.D5_PWM, J1.pulse
  N9: Part1.D6_PWM, J2.pulse
  N10: Part1.5V, R5.pin_1, R6.pin_1, R7.pin_1, R8.pin_1
  GND: IC1.GND, J1.gnd, J2.gnd, J3.gnd, J4.gnd, BAT1.-
  N11: IC1.IN, BAT1.+
  VCC: IC1.OUT, J1.vcc, J2.vcc, J3.vcc, J4.vcc

// code stored in the sketch: handcontrol.ino

//Define sensors and servos




#include <Servo.h> //Includes servo library



Servo finger1, finger2, finger3, finger4;



int servoPin1 = 5;

int servoPin2 = 6;

int servoPin3 = 9;

int servoPin4 = 10;



int flexPin1 = A0;

int flexPin2 = A1;

int flexPin3 = A2;

int flexPin4 = A3;

//int flexPin5 = A4;



void setup()

{

  //Attach the servo objects to their respective pins

  finger1.attach(servoPin1);

  finger2.attach(servoPin2);

  finger3.attach(servoPin3);

  finger4.attach(servoPin4);

  

  /* set each servo pin to output; I'm not acutally sure if this is

  even necessary, but I did just in case it is */

  pinMode(servoPin1, OUTPUT);

  pinMode(servoPin2, OUTPUT);

  pinMode(servoPin3, OUTPUT);

  pinMode(servoPin4, OUTPUT);

  

  //Set each flex sensor pin to input: this is necessary

  pinMode(flexPin1, INPUT);

  pinMode(flexPin2, INPUT);

  pinMode(flexPin3, INPUT);

  pinMode(flexPin4, INPUT);

  //pinMode(flexPin5, INPUT);

  

  finger1.write(90);

  finger2.write(90);

  finger3.write(90);

  finger4.write(90);

}



void loop()

{

  //Defines analog input variables

  int flex1 = analogRead(flexPin1);

  int flex2 = analogRead(flexPin2);

  int flex3 = analogRead(flexPin3);

  int flex4 = analogRead(flexPin4);

  //int flex5 = analogRead(flexPin5);

  

  /* Defines "pos" variables as being proportional to the flex inputs.

  The 400 to 700 value range seemed adequate for my sensors, but you can change

  yours accordingly. */

  int pos1 = map(flex1, 400, 600, 180, 0);

  pos1 = constrain(pos1, 0, 180);

  int pos2 = map(flex2, 500, 700, 180, 0);

  pos2 = constrain(pos2, 0, 180);

  int pos3 = map(flex3, 300, 610, 180, 0);

  pos3 = constrain(pos3, 0, 180);

  int pos4 = map(flex4, 400, 675, 180, 0);

  pos4 = constrain(pos4, 0, 180);

  //int pos5 = map(flex5, 400, 700, 180, 0);

  //pos5 = constrain(pos5, 0, 180);

  

  //Tells servos to move by the amount specified in the "pos" variables

  finger1.write(pos1); 

  finger2.write(pos2);

  finger3.write(pos3);

  finger4.write(pos4);

}
